# Fritzing sketch Untitled_Sketch (saved by Fritzing 0.9.3b)

parts:
  Composant2 = Arduino Uno (Rev3)
  Composant3 = HX711 Weighing Sensor Module

nets:
  N1: Composant2.A2, Composant3.DO/RX
  N2: Composant2.A3, Composant3.CK/TX
  5V: Composant2.5V, Composant3.VCC
  GND: Composant2.GND, Composant3.GND
